// Logisim project example2_13.circ as structural Verilog: 1 circuit, main circuit main
module main (
  input  C,
  input  A,
  input  B,
  output out_4
);

  wire not_1_out;

  not not_1 (not_1_out, C);
  Multiplexer #(.select(2)) multiplexer_1 (.in0(not_1_out), .in1(C), .in2(1'b1), .in3(1'b0), .out(out_4), .sel({A, B}));
endmodule
